// Logisim project Patient_Emergency_Alaram.circ as structural Verilog: 1 circuit, main circuit main
module main (
  input  A,
  input  Temp,
  input  C,
  input  BP,
  output Output__Y
);

  wire and_1_out, and_2_out, not_1_out;

  not not_1 (not_1_out, BP);
  buf and_1 (and_1_out, not_1_out);  // AND_Gate
  and and_2 (and_2_out, A, Temp, C);
  or or_1 (Output__Y, and_2_out, and_1_out);

  // Notes on the sheet:
  //   Heart Rate Low
  //   (HR)
  //   B
  //   Oxygen Level Low
  //   (Spo2)
  //   Blood Pressure Low
  //   D
  //   Body Temperature High
  //   NOT
  //   _
  //   D
  //   INPUTS
  //   OUTPUT
  //   Y - Alarm Output (0 = No Alarm, 1= Alarm)
  //   AND
  //   A - Heart Rate Low (0 = Normal,1 = Low)
  //    B - Body Temperature High (0 = Normal, 1 = High
  //   C - Oxygen Level Low (0 = Normal, 1 = Low)
  //   D - Blood Pressure Low (0 = Normal, 1 = Low)
  //   DIGITAL PATIENT EMERGENY ALARM AND ALTERT SYSYEM USING COMBINATIONAL LOGIC
  //   AND
  //   _
  //   D.A.B.C
  //   A.B.C
  //   SOFTWARE USED
  //   Logisim Evolution
  //   OR
  //   BOOLEAN EXPRESSION:
  //   Y = (A.B.C) + (D.A.B.C)
  //   COMPONENTS USED
  //    AND gates (2)
  //   OR gate (1)
  //   NOT gate (1)
  //    Input Switches (4)
  //   LED/ Alarm output (1)
  //   Connecting wires
  //   _
  //   Alarm
endmodule
